// Logisim project p0.Q1.circ as structural Verilog: 2 circuits, main circuit CRC
module CRC (
  input  [7:0] A1,
  input  [3:0] B,
  output [10:0] C
);

  wire [2:0] r1, r2, r3, r4, r5, r6, r7;

  mod2_divisor mod2_divisor_1 (.dividedNum(A1[7:4]), .divisor(B), .reminder(r1));
  mod2_divisor mod2_divisor_2 (.dividedNum({r1, A1[3]}), .divisor(B), .reminder(r2));
  mod2_divisor mod2_divisor_3 (.dividedNum({r2, A1[2]}), .divisor(B), .reminder(r3));
  mod2_divisor mod2_divisor_4 (.dividedNum({r3, A1[1]}), .divisor(B), .reminder(r4));
  mod2_divisor mod2_divisor_5 (.dividedNum({r4, A1[0]}), .divisor(B), .reminder(r5));
  mod2_divisor mod2_divisor_6 (.dividedNum({r5, 1'b0}), .divisor(B), .reminder(r6));
  mod2_divisor mod2_divisor_7 (.dividedNum({r6, 1'b0}), .divisor(B), .reminder(r7));
  mod2_divisor mod2_divisor_8 (.dividedNum({r7, 1'b0}), .divisor(B), .reminder(C[2:0]));

  assign C[10:3] = A1;

  // Other names for the same wires on the sheet: CRCcode[10:0] = {A1, C[2:0]}; final_quotient[2:0] = C[2:0];
  //   origin_frame[7:0] = A1; divisor[3:0] = B
endmodule

module mod2_divisor (
  input  [3:0] dividedNum,
  input  [3:0] divisor,
  output [2:0] reminder
);

  wire [2:0] bit_extender_1_out, bit_extender_2_out;
  wire [3:0] xor_1_out;

  assign xor_1_out = dividedNum ^ divisor;  // XOR_Gate xor_1, 4 bits wide
  Bit_Extender #(.in_width(4), .out_width(3)) bit_extender_1 (.in(dividedNum), .out(bit_extender_1_out));
  Bit_Extender #(.in_width(4), .out_width(3)) bit_extender_2 (.in(xor_1_out), .out(bit_extender_2_out));
  Multiplexer #(.width(3), .enable("false")) multiplexer_1 (
    .in0(bit_extender_1_out), .in1(bit_extender_2_out), .out(reminder), .sel(dividedNum[3]));

  // Other names for the same wires on the sheet: divideNum[3:0] = dividedNum; highest = dividedNum[3]
endmodule
