// Logisim project p0.Q3.circ as structural Verilog: 4 circuits, main circuit navigation
module navigation (
  input  [1:0] dir,
  input  clk,
  input  reset,
  output arrive,
  output hit
);

  wire counter_1_q, state_transition_1_arrive, state_transition_1_hit, state_transition_1_n0,
       state_transition_1_n1, state_transition_1_n2, state_transition_1_n3, state_transition_1_n4;
  wire [4:0] status, status_memory_1_status;

  state_transition state_transition_1 (
    .n4(state_transition_1_n4), .n3(state_transition_1_n3), .n2(state_transition_1_n2),
    .n1(state_transition_1_n1), .n0(state_transition_1_n0), .hit(state_transition_1_hit),
    .arrive(state_transition_1_arrive), .status(status), .dir(dir));
  status_memory status_memory_1 (
    .n4(state_transition_1_n4), .n3(state_transition_1_n3), .n2(state_transition_1_n2),
    .n1(state_transition_1_n1), .n0(state_transition_1_n0), .hit_next(state_transition_1_hit),
    .arrive_next(state_transition_1_arrive), .status(status_memory_1_status), .hit(hit), .arrive(arrive),
    .in_8(clk), .in_9(reset));
  Counter #(.width(1), .max('h1), .ongoal("stay")) counter_1 (
    .Q(counter_1_q), .clk(clk), .clr(reset));  // open: load, D, count, carry
  Multiplexer #(.width(5)) multiplexer_1 (
    .in0(5'b00001), .in1(status_memory_1_status), .out(status), .sel(counter_1_q));  // open: en

  // Other names for the same wires on the sheet: clr = reset
endmodule

module state_transition (
  input  [4:0] status,
  input  [1:0] dir,
  output n4,
  output n3,
  output n2,
  output n1,
  output n0,
  output hit,
  output arrive
);

  wire and_1_out, and_2_out, and_3_out, and_4_out, and_5_out, and_6_out, and_7_out, and_8_out, and_9_out,
       and_10_out, and_11_out, and_12_out, and_13_out, and_14_out, and_15_out, and_16_out, and_17_out,
       and_18_out, and_19_out, and_20_out, and_21_out, not_1_out, not_2_out, not_3_out, not_4_out, not_5_out,
       not_6_out, not_7_out, not_8_out, not_9_out, not_10_out, not_11_out, not_12_out, not_13_out,
       not_14_out, not_15_out, not_16_out, not_17_out, not_18_out, not_19_out, not_20_out, not_21_out,
       not_22_out, not_23_out, not_24_out, not_25_out, not_26_out, not_27_out, not_28_out, not_29_out,
       not_30_out, not_31_out, not_32_out, not_33_out, not_34_out, not_35_out, not_36_out, not_37_out,
       not_38_out, not_39_out, not_40_out, not_41_out, not_42_out, not_43_out, not_44_out, not_45_out;

  not not_1 (not_1_out, dir[1]);
  not not_2 (not_2_out, dir[0]);
  not not_3 (not_3_out, dir[1]);
  not not_4 (not_4_out, status[4]);
  not not_5 (not_5_out, status[2]);
  not not_6 (not_6_out, status[0]);
  not not_7 (not_7_out, dir[1]);
  not not_8 (not_8_out, dir[0]);
  not not_9 (not_9_out, status[4]);
  not not_10 (not_10_out, status[3]);
  not not_11 (not_11_out, status[0]);
  not not_12 (not_12_out, dir[1]);
  not not_13 (not_13_out, status[4]);
  not not_14 (not_14_out, status[3]);
  not not_15 (not_15_out, dir[1]);
  not not_16 (not_16_out, status[4]);
  not not_17 (not_17_out, status[3]);
  not not_18 (not_18_out, dir[1]);
  not not_19 (not_19_out, dir[0]);
  not not_20 (not_20_out, status[4]);
  not not_21 (not_21_out, status[3]);
  not not_22 (not_22_out, status[0]);
  not not_23 (not_23_out, dir[1]);
  not not_24 (not_24_out, dir[0]);
  not not_25 (not_25_out, dir[0]);
  not not_26 (not_26_out, status[3]);
  not not_27 (not_27_out, status[2]);
  not not_28 (not_28_out, status[1]);
  not not_29 (not_29_out, dir[0]);
  not not_30 (not_30_out, status[4]);
  not not_31 (not_31_out, status[3]);
  not not_32 (not_32_out, status[1]);
  not not_33 (not_33_out, dir[0]);
  not not_34 (not_34_out, status[4]);
  not not_35 (not_35_out, status[2]);
  not not_36 (not_36_out, status[4]);
  not not_37 (not_37_out, status[3]);
  not not_38 (not_38_out, status[1]);
  not not_39 (not_39_out, dir[1]);
  not not_40 (not_40_out, dir[1]);
  not not_41 (not_41_out, dir[1]);
  not not_42 (not_42_out, dir[0]);
  not not_43 (not_43_out, dir[1]);
  not not_44 (not_44_out, dir[0]);
  not not_45 (not_45_out, dir[1]);
  and and_1 (and_1_out, status[2], not_1_out, not_2_out);
  and and_2 (and_2_out, status[3], not_3_out, dir[0]);
  and and_3 (and_3_out, not_4_out, not_5_out, not_6_out, not_7_out, not_8_out);
  and and_4 (and_4_out, status[3], dir[1], dir[0]);
  and and_5 (and_5_out, not_9_out, not_10_out, not_11_out, not_12_out, dir[0]);
  and and_6 (and_6_out, not_13_out, not_14_out, status[1], not_15_out, dir[0]);
  and and_7 (and_7_out, not_16_out, not_17_out, status[2], not_18_out, dir[0]);
  and and_8 (and_8_out, status[2], dir[1], not_19_out);
  and and_9 (and_9_out, not_20_out, not_21_out, not_22_out, dir[1], dir[0]);
  and and_10 (and_10_out, status[0], not_23_out, not_24_out);
  and and_11 (and_11_out, status[3], dir[1], not_25_out);
  and and_12 (and_12_out, not_26_out, not_27_out, not_28_out, status[0], dir[0]);
  and and_13 (and_13_out, status[0], dir[1]);
  and and_14 (and_14_out, status[1], dir[1], not_29_out);
  and and_15 (and_15_out, not_30_out, not_31_out, not_32_out, dir[1], not_33_out);
  and and_16 (and_16_out, not_34_out, not_35_out, dir[1], dir[0]);
  and and_17 (and_17_out, not_36_out, not_37_out, not_38_out, status[0], not_39_out, dir[0]);
  and and_18 (and_18_out, status[2], not_40_out, dir[0]);
  and and_19 (and_19_out, status[3], not_41_out, not_42_out);
  and and_20 (and_20_out, status[2], not_43_out, not_44_out);
  and and_21 (and_21_out, status[3], not_45_out, dir[0]);
  or or_1 (n4, and_1_out, and_2_out);
  or or_2 (n3, and_3_out, and_4_out);
  or or_3 (n2, and_5_out, and_6_out, and_7_out, and_8_out);
  or or_4 (n1, and_9_out, and_10_out, and_11_out);
  or or_5 (n0, and_12_out, and_13_out, and_14_out, status[4]);
  or or_6 (hit, and_15_out, and_16_out, and_17_out, and_18_out, and_19_out);
  or or_7 (arrive, and_20_out, and_21_out);
endmodule

module status_memory (
  input  n4,
  input  n3,
  input  n2,
  input  n1,
  input  n0,
  input  hit_next,
  input  arrive_next,
  input  in_8,
  input  in_9,
  output [4:0] status,
  output hit,
  output arrive
);

  Register #(.width(5)) register_1 (.D({n4, n3, n2, n1, n0}), .Q(status), .clk(in_8), .clr(in_9));  // open: en
  Register #(.width(1)) register_2 (.D(hit_next), .Q(hit), .clk(in_8), .clr(in_9));  // open: en
  Register #(.width(1)) register_3 (.D(arrive_next), .Q(arrive), .clk(in_8), .clr(in_9));  // open: en

  // Other names for the same wires on the sheet: clk = in_8; clr = in_9
endmodule

module _1 (
  input  [4:0] status,
  input  [1:0] in_2
);
endmodule
