// Logisim project p0.Q4.circ as structural Verilog: 5 circuits, main circuit fsm
module fsm (
  input  clr,
  input  [1:0] in,
  output z
);

  wire clk, not_1_out, register_1_q, status_transition_1_n0, status_transition_1_n1, status_transition_1_n2,
       status_transition_1_n3, status_transition_1_n4;
  wire [4:0] status, status_memory_1_status;

  Clock clock_1 (.out(clk));
  status_transition status_transition_1 (
    .n4(status_transition_1_n4), .n3(status_transition_1_n3), .n2(status_transition_1_n2),
    .n1(status_transition_1_n1), .n0(status_transition_1_n0), .status(status), .in(in));
  status_memory status_memory_1 (
    .n4(status_transition_1_n4), .n3(status_transition_1_n3), .n2(status_transition_1_n2),
    .n1(status_transition_1_n1), .n0(status_transition_1_n0), .status(status_memory_1_status), .clk(clk));
  // Probe on status_memory_1_status
  not not_1 (not_1_out, clr);
  Multiplexer #(.width(5), .enable("false")) multiplexer_1 (
    .in0(5'b00001), .in1(status_memory_1_status), .out(status), .sel(register_1_q));
  Register #(.width(1)) register_1 (.D(not_1_out), .Q(register_1_q), .clk(clk));  // open: en, clr
  // Probe on status
  status_out status_out_1 (.in(in), .status(status), .z(z));
endmodule

module status_transition (
  input  [4:0] status,
  input  [1:0] in,
  output n4,
  output n3,
  output n2,
  output n1,
  output n0
);

  wire and_5_out, and_6_out, not_1_out, not_2_out, not_3_out, not_4_out, not_5_out, not_6_out, not_7_out,
       not_8_out, not_9_out, not_10_out, not_11_out, not_12_out, not_13_out, not_14_out, not_15_out,
       not_16_out;

  and and_1 (n4, status[3], not_1_out);
  not not_1 (not_1_out, in[0]);
  not not_2 (not_2_out, status[4]);
  not not_3 (not_3_out, status[3]);
  not not_4 (not_4_out, status[0]);
  not not_5 (not_5_out, in[0]);
  not not_6 (not_6_out, status[4]);
  not not_7 (not_7_out, status[3]);
  not not_8 (not_8_out, status[0]);
  not not_9 (not_9_out, in[1]);
  not not_10 (not_10_out, status[2]);
  not not_11 (not_11_out, status[1]);
  not not_12 (not_12_out, in[1]);
  not not_13 (not_13_out, status[3]);
  not not_14 (not_14_out, status[2]);
  not not_15 (not_15_out, status[1]);
  not not_16 (not_16_out, in[0]);
  and and_2 (n3, not_2_out, not_3_out, not_4_out, not_5_out);
  and and_3 (n2, not_6_out, not_7_out, not_8_out, not_9_out, in[0]);
  and and_4 (n1, not_10_out, not_11_out, not_12_out, in[0]);
  and and_5 (and_5_out, not_13_out, not_14_out, not_15_out, not_16_out);
  or or_1 (n0, and_5_out, and_6_out);
  and and_6 (and_6_out, in[1], in[0]);
endmodule

module status_memory (
  input  n4,
  input  n3,
  input  n2,
  input  n1,
  input  n0,
  input  clk,
  output [4:0] status
);

  Register #(.width(5)) register_1 (.D({n4, n3, n2, n1, n0}), .Q(status), .clk(clk));  // open: en, clr
endmodule

module status_out (
  input  [4:0] status,
  input  [1:0] in,
  output z
);

  wire bitselector_1_out, bitselector_2_out, not_1_out;

  BitSelector #(.width(5)) bitselector_1 (.in(status), .out(bitselector_1_out), .sel(3'b011));
  BitSelector #(.width(2)) bitselector_2 (.in(in), .out(bitselector_2_out), .sel(1'b0));
  not not_1 (not_1_out, bitselector_2_out);
  and and_1 (z, bitselector_1_out, not_1_out);
endmodule

module _1 (
  input  [4:0] status,
  input  [1:0] in
);
endmodule
