// Logisim project p0.Q5.circ as structural Verilog: 3 circuits, main circuit ftoi
module ftoi (
  input  [15:0] float,
  output [31:0] \int 
);

  wire [1:0] select_1_sel;
  wire [31:0] normalized;

  Normalized normalized_1 (.in_1(float[9:0]), .in_2(float[14:10]), .in_3(float[15]), .\int (normalized));
  select select_1 (.exponent(float[14:10]), .sel(select_1_sel));
  Multiplexer #(.select(2), .width(32)) multiplexer_1 (
    .in0(normalized), .in1({32{1'b0}}), .in2({32{1'b0}}), .in3({32{1'b0}}), .out(\int ), .sel(select_1_sel));  // open: en

  // Other names for the same wires on the sheet: frac[9:0] = float[9:0]; exponent[4:0] = float[14:10];
  //   sign = float[15]
endmodule

module select (
  input  [4:0] exponent,
  output [1:0] sel
);

  wire not_1_out, not_2_out, not_3_out, not_4_out, not_5_out;

  and and_1 (sel[1], exponent[4], exponent[3], exponent[2], exponent[1], exponent[0]);
  not not_1 (not_1_out, exponent[4]);
  not not_2 (not_2_out, exponent[3]);
  not not_3 (not_3_out, exponent[2]);
  not not_4 (not_4_out, exponent[1]);
  not not_5 (not_5_out, exponent[0]);
  and and_2 (sel[0], not_1_out, not_2_out, not_3_out, not_4_out, not_5_out);
endmodule

module Normalized (
  input  [9:0] in_1,
  input  [4:0] in_2,
  input  in_3,
  output [31:0] \int 
);

  wire sel;
  wire [4:0] subtractor_1_out;
  wire [10:0] bit_extender_1_out;
  wire [31:0] abs, adder_1_out, bit_extender_2_out, not_1_out, shifter_1_out, \signed ;

  // Probe on in_1
  Comparator #(.width(5), .mode("unsigned")) comparator_1 (.a(5'b01111), .b(in_2), .gt(sel));  // open: eq, lt
  // Probe on bit_extender_1_out
  assign bit_extender_1_out = {{1{1'b1}}, in_1};  // Bit_Extender bit_extender_1
  assign not_1_out = ~abs;  // NOT_Gate not_1, 32 bits wide
  assign bit_extender_2_out = {{21{1'b0}}, bit_extender_1_out};  // Bit_Extender bit_extender_2
  Subtractor #(.width(5)) subtractor_1 (.a(in_2), .b(5'b01111), .out(subtractor_1_out));  // open: bin, bout
  // Probe on subtractor_1_out
  Adder #(.width(32)) adder_1 (.a(not_1_out), .b(32'h1), .out(adder_1_out));  // open: cin, cout
  // Probe on bit_extender_2_out
  Shifter #(.width(32)) shifter_1 (.in(bit_extender_2_out), .\dist (subtractor_1_out), .out(shifter_1_out));
  Multiplexer #(.width(32)) multiplexer_1 (.in0(\signed ), .in1({32{1'b0}}), .out(\int ), .sel(sel));  // open: en
  // Probe on shifter_1_out
  // Probe on abs
  Shifter #(.width(32), .shift("lr")) shifter_2 (.in(shifter_1_out), .\dist (5'b01010), .out(abs));
  Multiplexer #(.width(32), .disabled(0), .enable("false")) multiplexer_2 (
    .in0(abs), .in1(adder_1_out), .out(\signed ), .sel(in_3));

  // Other names for the same wires on the sheet: exponent[4:0] = in_2; frac[9:0] = in_1; sign = in_3
endmodule
